# Fritzing sketch ThreadDripperV1 (saved by Fritzing 1.0.5)
breadboards: 1

parts:
  Part1 = Arduino Uno (Rev3) - ICSP
  Part2 = Soil Moisture Sensor
  Water_Level_Sensor1 = Water Level Sensor
  VEML1 = Light sensor VEML6070
  VEML2 = Light sensor VEML6070
  LCD2004-I2C1 = LCD2004-I2C
  L298N1 = L298N DC motor driver
  A1 = usbc to 12V module
  M1 = DC Motor [voltage_(max)=6V voltage_(min)=3V]

nets:
  N1: Part1.A0, Water_Level_Sensor1.SIG
  N2: Part1.A1, Part2.SIG
  5V: Part1.A4/SDA, VEML1.5V, VEML2.5V, LCD2004-I2C1.SDA
  GND: Part1.A5/SCL, VEML1.GND, VEML2.GND, LCD2004-I2C1.SCL
  GND_2: Part1.GND, Part2.GND, Water_Level_Sensor1.GND, VEML1.SCL, VEML2.SCL, LCD2004-I2C1.GND, L298N1.GND, A1.Pin_1, A1.Pin_2
  N3: Part1.D8, L298N1.IN2
  N4: Part1.D7, L298N1.IN1
  VCC: Part1.5V, Part2.VCC, Water_Level_Sensor1.VCC, VEML1.SDA, VEML2.SDA, LCD2004-I2C1.VCC
  VIN: Part1.VIN, L298N1.12V, A1.Pin_3, A1.Pin_4
  N5: L298N1.OUT1, M1.pin_2
  N6: L298N1.OUT2, M1.pin_1

notes:
  12v Power Delivery USB C
  12v Peristaltic Pump

custom parts:
  Water Level Sensor: A water level sensor. This sensor operates at 3V to 5V. The Sig (signal) pin outputs an analogue signal that is in proportion to the amount of water in contact with the sensor.
  LCD2004-I2C: A standard character display with 4x20 characters. Comes in many colors with LCM2004 IIC attached.
  L298N DC motor driver: 2x DC motor driver with 78M05 positive voltage regulator (7..35 V) L298N: max 46 V, 2 A Set 5 V Enable jumper to enable 5 V regultor (needed for the L298N) and +5 V output at screw terminal or supply external +5 V at screw terminal Set ENA and/or ENB to +5 V to enable motor permanently or supply ENA and/or ENB with PWM signal IN1 and IN2 set rotation directory for motor A (OUT1/OUT2) IN2 and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
  usbc to 12V module: usbc to 12V module.
